# Fritzing sketch ultimo archivo (saved by Fritzing 0.9.3b)
circuit board: 10.7669cm x 5.78324cm

parts:
  KY-1 = Keyes Relay [package=THT]
  Componente2 = Bluetooth HC-05 Macho
  Componente1 = Arduino Mega ADK (Rev3)

nets:
  N1: KY-1.signal, Componente1.D2_PWM
  VCC: KY-1.power, Componente2.VCC, Componente1.IOREF, Componente1.5V
  GND: KY-1.ground, Componente2.GND, Componente1.GND
  N2: KY-1.C, KY-1.NO
  N3: Componente2.TXD, Componente1.D0/RX0
  N4: Componente2.RXD, Componente1.D1/TX0

custom parts:
  Keyes Relay: The Keyes 5V relay module is suitable for SCM development, home appliance control. It uses a 5V~12V TIL control signal which can control DC / AC signal.
